# Fritzing sketch 旋转编码器控制电机速度 (saved by Fritzing 0.9.9b)
breadboards: 1

parts:
  M1 = STM32F103C8T6 blue mini board
  M2 = motor driver shz-mdbl-010 [package=THT]
  Grove1 = Grove OLED 128x96
  RE1 = Rotary Encoder [package=THT]
  M3 = DC Motor
  A1 = STLINK

nets:
  N1: M1.B8, Grove1.SCL
  N2: M1.B9, Grove1.SDA
  N3: M1.G, M1.GND, M2.pin_6, RE1.SwitchPinE, A1.Pin_3, A1.Pin_4
  N4: M1.3.3V, M1.3.3, RE1.SwitchrPinD, A1.Pin_7, A1.Pin_8
  N5: M1.A1, M2.pin_9
  N6: M1.A2, M2.pin_10
  N7: M1.B0, RE1.EncoderPinA
  N8: M1.B1, RE1.EncoderPinB
  N9: M1.DIO, A1.Pin_2
  N10: M1.CLK, A1.Pin_6
  N11: M2.pin_1, M3.pin_2
  N12: M2.pin_2, M3.pin_1
  N13: M2.pin_5, A1.Pin_9, A1.Pin_10

custom parts:
  motor driver shz-mdbl-010: Motor drive module is ideal for use in battery-powered smart car, toy cars, robots. Supply voltage 2V ~ 10V, can drive two DC motors or a 4-wire 2-phase stepper motors ,can achieve forward rotation or reverse rotation, it is possible to adjust the rotation speed. Each can provide continuous current of 1.5A, peak current up to 2.5A, thermal protection and can be automatically restored.
  Rotary Encoder: Rotary Encoder from ALPSec11e with switch.
  STLINK: STLINK.
